# Fritzing sketch AnalogLEDs+Multiplexer (saved by Fritzing 0.9.3b)
breadboards: 4

parts:
  Part1 = Analog Digital MUX Breakout  # not connected
  Part2 = Analog Digital MUX Breakout  # not connected
  Q1 = Basic FET N-Channel [package="TO220 [THT]"]  # not connected
  Q2 = Basic FET N-Channel [package="TO220 [THT]"]  # not connected
  Q3 = Basic FET N-Channel [package="TO220 [THT]"]  # not connected
  Q4 = Basic FET N-Channel [package="TO220 [THT]"]  # not connected
  Q5 = Basic FET N-Channel [package="TO220 [THT]"]  # not connected
  Q6 = Basic FET N-Channel [package="TO220 [THT]"]  # not connected
  Q7 = Basic FET N-Channel [package="TO220 [THT]"]  # not connected
  Q8 = Basic FET N-Channel [package="TO220 [THT]"]  # not connected
  Q9 = Basic FET N-Channel [package="TO220 [THT]"]  # not connected
  Q10 = Basic FET N-Channel [package="TO220 [THT]"]  # not connected
  R1 = Resistor [tolerance=±5% resistance=10k package="0402 [SMD]"]
  R2 = Resistor [tolerance=±5% resistance=10k package="0402 [SMD]"]
  R3 = Resistor [tolerance=±5% resistance=10k package="0402 [SMD]"]
  R4 = Resistor [tolerance=±5% resistance=10k package="0402 [SMD]"]
  R5 = Resistor [tolerance=±5% resistance=10k package="0402 [SMD]"]
  R6 = Resistor [tolerance=±5% resistance=10k package="0402 [SMD]"]
  R7 = Resistor [tolerance=±5% resistance=10k package="0402 [SMD]"]
  R8 = Resistor [tolerance=±5% resistance=10k package="0402 [SMD]"]
  R9 = Resistor [tolerance=±5% resistance=10k package="0402 [SMD]"]
  R10 = Resistor [tolerance=±5% resistance=10k package="0402 [SMD]"]
  Part3 = Arduino Uno (Rev3)  # not connected
  Q11 = Basic FET N-Channel [package="TO220 [THT]"]  # not connected
  Q12 = Basic FET N-Channel [package="TO220 [THT]"]  # not connected
  Q13 = Basic FET N-Channel [package="TO220 [THT]"]  # not connected
  Q14 = Basic FET N-Channel [package="TO220 [THT]"]  # not connected
  Q15 = Basic FET N-Channel [package="TO220 [THT]"]  # not connected
  Q16 = Basic FET N-Channel [package="TO220 [THT]"]  # not connected
  Q17 = Basic FET N-Channel [package="TO220 [THT]"]  # not connected
  Q18 = Basic FET N-Channel [package="TO220 [THT]"]  # not connected
  Q19 = Basic FET N-Channel [package="TO220 [THT]"]  # not connected
  Q20 = Basic FET N-Channel [package="TO220 [THT]"]  # not connected
  R11 = Resistor [tolerance=±5% resistance=10k package="0402 [SMD]"]
  R12 = Resistor [tolerance=±5% resistance=10k package="0402 [SMD]"]
  R13 = Resistor [tolerance=±5% resistance=10k package="0402 [SMD]"]
  R14 = Resistor [tolerance=±5% resistance=10k package="0402 [SMD]"]
  R15 = Resistor [tolerance=±5% resistance=10k package="0402 [SMD]"]
  R16 = Resistor [tolerance=±5% resistance=10k package="0402 [SMD]"]
  R17 = Resistor [tolerance=±5% resistance=10k package="0402 [SMD]"]
  R18 = Resistor [tolerance=±5% resistance=10k package="0402 [SMD]"]
  R19 = Resistor [tolerance=±5% resistance=10k package="0402 [SMD]"]
  R20 = Resistor [tolerance=±5% resistance=10k package="0402 [SMD]"]

nets:
  N1: R1.Pin_1, R2.Pin_1, R3.Pin_1, R4.Pin_1, R5.Pin_1, R6.Pin_1, R7.Pin_1, R8.Pin_1, R9.Pin_1, R10.Pin_1
  N2: R11.Pin_0, R12.Pin_0, R13.Pin_0, R14.Pin_0, R15.Pin_0, R16.Pin_0, R17.Pin_0, R18.Pin_0, R19.Pin_0, R20.Pin_0

notes:
  12 V 5 A Power Supply needed
