# Fritzing sketch AnalogLEDs+Multiplexer copy (saved by Fritzing 0.9.3b)
breadboards: 1

parts:
  Part3 = Arduino Uno (Rev3)  # not connected
  R1 = Rotary Potentiometer (Small) [maximum_resistance=100kΩ package=THT]
  S2 = Toggle Switch [package=THT]

nets:
  N1: R1.leg1, R1.wiper, R1.leg2
  N2: S2.L1, S2.COM

notes:
  12 V 5 A Power Supply needed
