# Fritzing sketch NeoPixelStripControl (saved by Fritzing 0.9.3b)
breadboards: 1

parts:
  Part3 = Arduino Uno (Rev3)
  R1 = Rotary Potentiometer (Small) [maximum_resistance=300Ω package=THT]
  S2 = Toggle Switch [package=THT]
  R2 = Resistor [tolerance=±5% resistance=220 package=THT]
  R3 = Resistor [tolerance=±5% resistance=220 package=THT]
  NEOPIXEL1 = Neopixel Strip -- White (30/m)
  NEOPIXEL2 = Neopixel Strip -- White (30/m)
  JACK1 = 2.1mm Barrel Jack with Terminal Block
  C1 = Electrolytic Capacitor [capacitance=1µF voltage=25V package="100 mil [THT, electrolytic]"]

nets:
  N1: Part3.A2, S2.COM
  GND: Part3.GND, S2.L2, R2.Pin_1, NEOPIXEL2.GND
  N2: Part3.D3_PWM, R1.wiper
  N3: Part3.D6_PWM, R3.Pin_1
  N4: Part3.5V, R1.leg1, S2.L1
  N5: R1.leg2, R2.Pin_0
  N6: R3.Pin_0, NEOPIXEL2.Dout
  N7: NEOPIXEL1.+5V, JACK1.POS, C1.+
  N8: NEOPIXEL1.GND, JACK1.NEG

notes:
  5.5 Volt Power Supply

custom parts:
  Neopixel Strip -- White (30/m): These NeoPixel strips have 30 digitally-addressable pixel LEDs per meter and are very affordable and are only 12.5 mm wide, 10 mm if you remove the strip from the casing.
